// Logisim project UniversalShiftRegister.circ as structural Verilog: 1 circuit, main circuit main
module main (
  input  I0,
  input  I1,
  input  I2,
  input  I3,
  input  [1:0] selection,
  input  D,
  output Q0,
  output Q1,
  output Q2,
  output Q3
);

  wire clock_1_out, multiplexer_1_out, multiplexer_2_out, multiplexer_3_out, multiplexer_4_out;

  Clock clock_1 (.out(clock_1_out));
  Multiplexer #(.select(2)) multiplexer_1 (
    .in0(D), .in1(I0), .in2(Q0), .in3(Q1), .out(multiplexer_1_out), .sel(selection));
  D_Flip_Flop d_ff_1 (.D(multiplexer_1_out), .clk(clock_1_out), .Q(Q0));  // open: Qn, preset, reset
  Multiplexer #(.select(2)) multiplexer_2 (
    .in0(Q0), .in1(I1), .in2(Q1), .in3(Q2), .out(multiplexer_2_out), .sel(selection));
  D_Flip_Flop d_ff_2 (.D(multiplexer_2_out), .clk(clock_1_out), .Q(Q1));  // open: Qn, preset, reset
  Multiplexer #(.select(2)) multiplexer_3 (
    .in0(Q1), .in1(I2), .in2(Q2), .in3(Q3), .out(multiplexer_3_out), .sel(selection));
  D_Flip_Flop d_ff_3 (.D(multiplexer_3_out), .clk(clock_1_out), .Q(Q2));  // open: Qn, preset, reset
  Multiplexer #(.select(2)) multiplexer_4 (
    .in0(Q2), .in1(I3), .in2(Q3), .in3(D), .out(multiplexer_4_out), .sel(selection));
  D_Flip_Flop d_ff_4 (.D(multiplexer_4_out), .clk(clock_1_out), .Q(Q3));  // open: Qn, preset, reset
endmodule
