// Logisim project decoder3to8.circ as structural Verilog: 1 circuit, main circuit main
module main (
  input  in_1,
  input  in_2,
  input  in_3,
  input  in_4,
  input  in_5,
  input  in_6,
  input  in_7,
  input  in_8,
  input  in_9,
  input  i3,
  input  in_11,
  input  in_12,
  input  in_13,
  input  in_14,
  output _0,
  output _1,
  output _2,
  output _3,
  output out_19,
  output _4,
  output _5,
  output _6,
  output _7
);

  wire and_9_out, and_10_out, and_11_out, and_12_out, and_13_out, and_14_out, and_15_out, and_16_out,
       not_1_out, not_2_out, not_3_out, not_4_out, not_5_out, not_6_out;

  not not_1 (not_1_out, in_1);
  not not_2 (not_2_out, in_2);
  not not_3 (not_3_out, in_3);
  and and_1 (_0, not_3_out, not_2_out, not_1_out);
  and and_2 (_1, in_3, not_2_out, not_1_out);
  and and_3 (_2, not_3_out, in_2, not_1_out);
  and and_4 (_3, in_3, in_2, not_1_out);
  and and_5 (_4, not_3_out, not_2_out, in_1);
  and and_6 (_5, in_3, not_2_out, in_1);
  and and_7 (_6, not_3_out, in_2, in_1);
  and and_8 (_7, in_3, in_2, in_1);
  not not_4 (not_4_out, in_4);
  not not_5 (not_5_out, in_5);
  not not_6 (not_6_out, in_6);
  and and_9 (and_9_out, not_6_out, not_5_out, not_4_out, in_7);
  and and_10 (and_10_out, in_6, not_5_out, not_4_out, in_8);
  and and_11 (and_11_out, not_6_out, in_5, in_9, not_4_out);
  and and_12 (and_12_out, in_6, in_5, i3, not_4_out);
  and and_13 (and_13_out, not_6_out, not_5_out, in_11, in_4);
  and and_14 (and_14_out, in_6, not_5_out, in_12, in_4);
  and and_15 (and_15_out, not_6_out, in_5, in_13, in_4);
  and and_16 (and_16_out, in_6, in_5, in_14, in_4);
  or or_1 (out_19, and_9_out, and_10_out, and_16_out, and_11_out, and_12_out, and_13_out, and_15_out, and_14_out);

  // Notes on the sheet:
  //   A
  //   B
  //   C
  //   i4
  //   i5
  //   i6
  //   i7
  //   i0
  //   i1
  //   i2
  //   S2
  //   S1
  //   S0
  //   Output
endmodule
