// Logisim project q3.circ as structural Verilog: 5 circuits, main circuit main
module main (
  input  k2,
  input  k1,
  input  k0,
  input  in_4,
  input  c2,
  input  c1,
  input  c0,
  input  in_8,
  output C___K,
  output C___K_2,
  output K___C
);

  wire encod_1_o0, encod_1_o1, encod_2_o0, encod_2_o1;

  encod encod_1 (.i3(c2), .i2(c1), .i1(c0), .i0(in_8), .o1(encod_1_o1), .o0(encod_1_o0));
  encod encod_2 (.i3(k2), .i2(k1), .i1(k0), .i0(in_4), .o1(encod_2_o1), .o0(encod_2_o0));
  Equality equality_1 (.c0(encod_1_o0), .c1(encod_1_o1), .k0(encod_2_o0), .k1(encod_2_o1), .E(C___K));
  compare compare_1 (.k1(encod_2_o1), .k0(encod_2_o0), .c1(encod_1_o1), .c0(encod_1_o0), .cLTk(K___C));
  compareKltC comparekltc_1 (.k1(encod_2_o1), .k0(encod_2_o0), .c1(encod_1_o1), .c0(encod_1_o0), .kLTc(C___K_2));

  // Notes on the sheet:
  //   k3
  //   c3
  //   4 : 2 encoder
  //   4 : 2 encoder
endmodule

module Equality (
  input  c0,
  input  c1,
  input  k0,
  input  k1,
  output E
);

  wire xnor_1_out, xnor_2_out;

  xnor xnor_1 (xnor_1_out, c0, k0);
  xnor xnor_2 (xnor_2_out, c1, k1);
  and and_1 (E, xnor_1_out, xnor_2_out);
endmodule

module encod (
  input  i3,
  input  i2,
  input  i1,
  input  i0,
  output o1,
  output o0
);

  or or_1 (o0, i1, i3);
  or or_2 (o1, i2, i3);
endmodule

module compare (
  input  k1,
  input  k0,
  input  c1,
  input  c0,
  output cLTk
);

  wire and_1_out, and_2_out, and_3_out, not_1_out, not_2_out, not_3_out, not_4_out, xnor_1_out;

  not not_1 (not_1_out, k1);
  not not_2 (not_2_out, k0);
  not not_3 (not_3_out, c1);
  not not_4 (not_4_out, c0);
  and and_1 (and_1_out, not_3_out, k1);
  xnor xnor_1 (xnor_1_out, c1, k1);
  and and_2 (and_2_out, not_4_out, k0);
  and and_3 (and_3_out, xnor_1_out, and_2_out);
  or or_1 (cLTk, and_1_out, and_3_out);
endmodule

module compareKltC (
  input  k1,
  input  k0,
  input  c1,
  input  c0,
  output kLTc
);

  wire and_1_out, and_2_out, and_3_out, not_1_out, not_2_out, not_3_out, not_4_out, xnor_1_out;

  not not_1 (not_1_out, k1);
  not not_2 (not_2_out, k0);
  not not_3 (not_3_out, c1);
  not not_4 (not_4_out, c0);
  and and_1 (and_1_out, not_1_out, c1);
  xnor xnor_1 (xnor_1_out, c1, k1);
  and and_2 (and_2_out, not_2_out, c0);
  and and_3 (and_3_out, xnor_1_out, and_2_out);
  or or_1 (kLTc, and_1_out, and_3_out);
endmodule
