// Logisim project FA_using_Modules.circ as structural Verilog: 3 circuits, main circuit main
module main (
  input  [3:0] X,
  input  [3:0] Y,
  input  Cin,
  input  in_4
);

  wire and_1_out, and_2_out, fulladder4bit_1_cout;
  wire [2:2] or_1_out;
  wire [3:0] fulladder4bit_1_s, fulladder4bit_2_s;

  Hex_Digit_Display hex_digit_display_1 (.value(X));  // open: dp
  or or_1 (or_1_out[2], fulladder4bit_1_cout, and_1_out, and_2_out);
  Hex_Digit_Display hex_digit_display_2 (.value(Y));  // open: dp
  and and_1 (and_1_out, fulladder4bit_1_s[3], fulladder4bit_1_s[2]);
  and and_2 (and_2_out, fulladder4bit_1_s[3], fulladder4bit_1_s[1]);
  Hex_Digit_Display hex_digit_display_3 (.value({{3{in_4}}, or_1_out[2]}));  // open: dp
  FullAdder4Bit fulladder4bit_1 (.X(X), .Y(Y), .Cin(Cin), .Cout(fulladder4bit_1_cout), .S(fulladder4bit_1_s));
  FullAdder4Bit fulladder4bit_2 (
    .X(fulladder4bit_1_s), .Y({in_4, {2{or_1_out[2]}}, in_4}), .Cin(in_4), .S(fulladder4bit_2_s));  // open: Cout
  Hex_Digit_Display hex_digit_display_4 (.value(fulladder4bit_2_s));  // open: dp

  // Notes on the sheet:
  //   +
endmodule

module fullAdder (
  input  X,
  input  Y,
  input  Cin,
  output S,
  output Cout
);

  wire and_1_out, and_2_out, xor_1_out;

  xor xor_1 (xor_1_out, X, Y);
  and and_1 (and_1_out, X, Y);
  xor xor_2 (S, xor_1_out, Cin);
  and and_2 (and_2_out, xor_1_out, Cin);
  or or_1 (Cout, and_2_out, and_1_out);
endmodule

module FullAdder4Bit (
  input  [3:0] X,
  input  [3:0] Y,
  input  Cin,
  output Cout,
  output [3:0] S
);

  wire fulladder_2_cout, fulladder_3_cout, fulladder_4_cout;

  fullAdder fulladder_1 (.X(X[3]), .Y(Y[3]), .Cin(fulladder_2_cout), .S(S[3]), .Cout(Cout));
  fullAdder fulladder_2 (.X(X[2]), .Y(Y[2]), .Cin(fulladder_3_cout), .S(S[2]), .Cout(fulladder_2_cout));
  fullAdder fulladder_3 (.X(X[1]), .Y(Y[1]), .Cin(fulladder_4_cout), .S(S[1]), .Cout(fulladder_3_cout));
  fullAdder fulladder_4 (.X(X[0]), .Y(Y[0]), .Cin(Cin), .S(S[0]), .Cout(fulladder_4_cout));
endmodule
