// Logisim project GRAYCODE_AND_BINARY_CONVERTERS.circ as structural Verilog: 1 circuit, main circuit main
module main (
  input  G3,
  input  G2,
  input  G1,
  input  G0,
  input  B3,
  input  B2,
  input  B1,
  input  B0,
  output B3_2,
  output B2_2,
  output B1_2,
  output B0_2,
  output G3_2,
  output G2_2,
  output G1_2,
  output G0_2
);

  Hex_Digit_Display hex_digit_display_1 (.value({G3, G2, G1, G0}));  // open: dp
  Hex_Digit_Display hex_digit_display_2 (.value({B3, B2, B1, B0}));  // open: dp
  xor xor_1 (B2_2, G2, G3);
  xor xor_2 (B1_2, G1, B2_2);
  xor xor_3 (G0_2, B0, B1);
  xor xor_4 (G1_2, B1, B2);
  xor xor_5 (G2_2, B2, B3);
  xor xor_6 (B0_2, G0, B1_2);
  Hex_Digit_Display hex_digit_display_3 (.value({B3, G2_2, G1_2, G0_2}));  // open: dp
  Hex_Digit_Display hex_digit_display_4 (.value({G3, B2_2, B1_2, B0_2}));  // open: dp

  assign B3_2 = G3;
  assign G3_2 = B3;
endmodule
