// Logisim project Q1.circ as structural Verilog: 1 circuit, main circuit main
module main (
  input  A,
  input  B,
  input  C,
  output out_4
);

  wire and_1_out, and_2_out, and_3_out, and_4_out, and_5_out, and_6_out, and_7_out, not_1_out, not_2_out,
       not_3_out, or_1_out, or_2_out;

  not not_1 (not_1_out, A);
  not not_2 (not_2_out, B);
  not not_3 (not_3_out, C);
  and and_1 (and_1_out, not_1_out, not_2_out);
  and and_2 (and_2_out, A, B);
  and and_3 (and_3_out, not_1_out, B);
  and and_4 (and_4_out, and_1_out, C);
  and and_5 (and_5_out, and_2_out, not_3_out);
  and and_6 (and_6_out, and_3_out, not_3_out);
  and and_7 (and_7_out, and_1_out, not_3_out);
  or or_1 (or_1_out, and_4_out, and_5_out);
  or or_2 (or_2_out, and_6_out, and_7_out);
  or or_3 (out_4, or_1_out, or_2_out);
  LED led_1 (.in(out_4));

  // Notes on the sheet:
  //   A'B'
  //   AB
  //   A'B
  //   ABC'
  //   A'BC'
  //   A'B'C'
  //   A'B'C
  //   A'B'C + ABC'
  //   A'BC' + A'B'C'
  //   A'B'C'+ABC'+A'BC'+A'B'C'
endmodule
