// Logisim project Q4.circ as structural Verilog: 1 circuit, main circuit main
module main (
  input  A,
  input  B,
  input  C,
  input  D
);

  wire ABD_out, and_1_out, and_2_out, and_3_out, and_4_out, and_5_out, and_6_out, BCD_out, CD_out, not_1_out,
       not_2_out, not_3_out, or_1_out, or_2_out, or_3_out, or_4_out;

  not not_1 (not_1_out, A);
  not not_2 (not_2_out, B);
  not not_3 (not_3_out, C);
  and and_1 (and_1_out, A, B);
  and and_2 (and_2_out, not_1_out, not_2_out);
  and and_3 (and_3_out, not_3_out, D);
  and CD (CD_out, C, D);
  and and_4 (and_4_out, and_1_out, not_3_out);
  and and_5 (and_5_out, and_2_out, and_3_out);
  and and_6 (and_6_out, and_1_out, CD_out);
  and BCD (BCD_out, CD_out, B);
  and ABD (ABD_out, and_1_out, D);
  or or_1 (or_1_out, and_4_out, and_5_out);
  or or_2 (or_2_out, and_6_out, BCD_out);
  or or_3 (or_3_out, or_2_out, ABD_out);
  or or_4 (or_4_out, or_1_out, or_3_out);
  LED led_1 (.in(or_4_out));

  // Notes on the sheet:
  //   AB
  //   A'B'
  //   C'D
  //   ABC'
  //   A'B'C'D
  //   ABCD
  //   ABC' + A'B'C'D
  //   ABCD + BCD
  //   ABCD+BCD+ABD
  //   ABC'+A'B'C'D+ABCD+BCD+ABD
endmodule
