// Logisim project LookForwardAdder.circ as structural Verilog: 1 circuit, main circuit main
module main (
  input  c0,
  input  [3:0] x,
  input  [3:0] y,
  input  in_4,
  output s0,
  output c1,
  output s1,
  output c2,
  output s2,
  output c3,
  output s3,
  output c4
);

  wire and_1_out, and_2_out, and_3_out, and_4_out, and_5_out, and_6_out, and_7_out, and_8_out, and_9_out,
       g0_out, g1_out, g2_out, g3_out, p0_out, p0c0_out, p1_out, p2_out, p3_out;

  xor p0 (p0_out, x[0], y[0]);
  and g0 (g0_out, x[0], y[0]);
  xor p1 (p1_out, x[1], y[1]);
  and g1 (g1_out, x[1], y[1]);
  xor p2 (p2_out, x[2], y[2]);
  and g2 (g2_out, x[2], y[2]);
  xor p3 (p3_out, x[3], y[3]);
  and g3 (g3_out, x[3], y[3]);
  and p0c0 (p0c0_out, c0, p0_out);
  and and_1 (and_1_out, p0_out, c0, p1_out);
  and and_2 (and_2_out, p1_out, g0_out);
  and and_3 (and_3_out, p0_out, p1_out, p2_out, c0);
  and and_4 (and_4_out, p2_out, p1_out, g0_out);
  and and_5 (and_5_out, p2_out, g1_out);
  and and_6 (and_6_out, p0_out, p1_out, p2_out, p3_out, c0);
  and and_7 (and_7_out, p1_out, p2_out, p3_out, g0_out);
  and and_8 (and_8_out, p2_out, p3_out, g1_out);
  and and_9 (and_9_out, p3_out, g2_out);
  xor xor_1 (s0, p0_out, c0);
  xor xor_2 (s1, p1_out, c1);
  xor xor_3 (s2, p2_out, c2);
  xor xor_4 (s3, p3_out, c3);
  or or_1 (c1, p0c0_out, g0_out);
  or or_2 (c2, and_1_out, and_2_out, g1_out);
  or or_3 (c4, and_6_out, and_7_out, and_8_out, and_9_out, g3_out);
  or or_4 (c3, and_3_out, and_4_out, and_5_out, g2_out);
  Hex_Digit_Display hex_digit_display_1 (.value({{3{in_4}}, c4}));  // open: dp
  Hex_Digit_Display hex_digit_display_2 (.value({s3, s2, s1, s0}));  // open: dp

  // Notes on the sheet:
  //   g0
  //   p1.p0.c0
  //   p1.g0
  //   p2.p1.p0.c0
  //   p2.p1.g0
  //   p2.g1
  //   p3.p2.p1.p0.c0
  //   p3.p2.p1.g0
  //   p3.p2.g1
  //   p3.g2
  //   s0
  //   s1
  //   c1
endmodule
