// Logisim project FA_and_FSFA.circ as structural Verilog: 1 circuit, main circuit main
module main (
  input  in_1,
  input  in_2,
  input  [3:0] in_3,
  input  [3:0] in_4,
  input  [3:0] in_5,
  input  [3:0] in_6,
  input  in_7,
  input  in_8,
  input  in_9,
  input  in_10,
  input  in_11,
  input  in_12,
  output C4,
  output out_14,
  output out_15,
  output out_16,
  output out_17,
  output out_18,
  output out_19,
  output out_20,
  output out_21,
  output out_22
);

  wire and_1_out, and_2_out, and_3_out, and_4_out, and_5_out, and_6_out, and_7_out, and_8_out, and_9_out,
       and_10_out, and_11_out, and_12_out, and_13_out, and_14_out, and_15_out, and_16_out, or_1_out,
       or_2_out, or_3_out, or_5_out, or_6_out, or_7_out, xor_1_out, xor_2_out, xor_3_out, xor_4_out,
       xor_9_out, xor_10_out, xor_11_out, xor_12_out, xor_13_out, xor_14_out, xor_15_out, xor_16_out;
  wire [0:0] xor_21_out;

  xor xor_1 (xor_1_out, in_5[0], in_6[0]);
  and and_1 (and_1_out, in_5[0], in_6[0]);
  xor xor_2 (xor_2_out, in_5[1], in_6[1]);
  and and_2 (and_2_out, in_5[1], in_6[1]);
  xor xor_3 (xor_3_out, in_5[2], in_6[2]);
  and and_3 (and_3_out, in_5[2], in_6[2]);
  xor xor_4 (xor_4_out, in_5[3], in_6[3]);
  and and_4 (and_4_out, in_5[3], in_6[3]);
  xor xor_5 (out_22, xor_1_out, in_2);
  and and_5 (and_5_out, xor_1_out, in_2);
  xor xor_6 (out_21, xor_2_out, or_1_out);
  and and_6 (and_6_out, xor_2_out, or_1_out);
  xor xor_7 (out_20, xor_3_out, or_2_out);
  and and_7 (and_7_out, xor_3_out, or_2_out);
  xor xor_8 (out_19, xor_4_out, or_3_out);
  and and_8 (and_8_out, xor_4_out, or_3_out);
  or or_1 (or_1_out, and_5_out, and_1_out);
  or or_2 (or_2_out, and_6_out, and_2_out);
  or or_3 (or_3_out, and_7_out, and_3_out);
  or or_4 (out_18, and_8_out, and_4_out);
  Hex_Digit_Display hex_digit_display_1 (.value({{2{in_10}}, in_8, out_18}));  // open: dp
  Hex_Digit_Display unit (.value({out_19, out_20, out_21, out_22}));  // open: dp
  xor xor_9 (xor_9_out, in_4[0], in_1);
  xor xor_10 (xor_10_out, in_4[1], in_1);
  xor xor_11 (xor_11_out, in_4[2], in_1);
  xor xor_12 (xor_12_out, in_4[3], in_1);
  xor xor_13 (xor_13_out, xor_9_out, in_3[0]);
  and and_9 (and_9_out, xor_9_out, in_3[0]);
  xor xor_14 (xor_14_out, xor_10_out, in_3[1]);
  and and_10 (and_10_out, xor_10_out, in_3[1]);
  xor xor_15 (xor_15_out, xor_11_out, in_3[2]);
  and and_11 (and_11_out, xor_11_out, in_3[2]);
  xor xor_16 (xor_16_out, xor_12_out, in_3[3]);
  and and_12 (and_12_out, xor_12_out, in_3[3]);
  xor xor_17 (out_17, xor_13_out, in_1);
  and and_13 (and_13_out, xor_13_out, in_1);
  xor xor_18 (out_16, xor_14_out, or_5_out);
  and and_14 (and_14_out, xor_14_out, or_5_out);
  xor xor_19 (out_15, xor_15_out, or_6_out);
  and and_15 (and_15_out, xor_15_out, or_6_out);
  xor xor_20 (out_14, xor_16_out, or_7_out);
  and and_16 (and_16_out, xor_16_out, or_7_out);
  or or_5 (or_5_out, and_13_out, and_9_out);
  or or_6 (or_6_out, and_14_out, and_10_out);
  or or_7 (or_7_out, and_15_out, and_11_out);
  or or_8 (C4, and_16_out, and_12_out);
  xor xor_21 (xor_21_out[0], C4, in_1);
  Hex_Digit_Display hex_digit_display_2 (.value({{2{in_9}}, in_7, xor_21_out[0]}));  // open: dp
  Hex_Digit_Display hex_digit_display_3 (.value({out_14, out_15, out_16, out_17}));  // open: dp

  assign in_11 = in_9;
  assign in_12 = in_10;

  // Notes on the sheet:
  //   X
  //   Y
  //   C0
  //   C1
  //   C2
  //   C3
  //   C4
  //   S2
  //   S3
  //   S1
  //   S0
  //   Y
  //   X
  //   C0
  //   C1
  //   C2
  //   C3
  //   S2
  //   S3
  //   S1
  //   S0
endmodule
